# Fritzing sketch esp8266 (saved by Fritzing 0.9.3b)
breadboards: 1

parts:
  BME280_(SPI1) = BME280 Breakout
  STM32_Blue_Pill = STM32F103C8T6 blue mini board
  U1 = ESP8266 WiFi Module [part_number=ESP8266]  # not connected

nets:
  N1: BME280_(SPI1).!CS, STM32_Blue_Pill.B6
  N2: BME280_(SPI1).SDI/SDA, STM32_Blue_Pill.B9
  N3: BME280_(SPI1).SDO/ADR, STM32_Blue_Pill.B8
  N4: BME280_(SPI1).SCK/SCL, STM32_Blue_Pill.B7
  N5: BME280_(SPI1).3.3V, STM32_Blue_Pill.A12
  N6: BME280_(SPI1).GND, STM32_Blue_Pill.A11
  N7: STM32_Blue_Pill.G, STM32_Blue_Pill.VBAT, STM32_Blue_Pill.GND
  N8: STM32_Blue_Pill.3.3V, STM32_Blue_Pill.3.3

notes:
  SPI1

custom parts:
  ESP8266 WiFi Module: Generic WiFi Module based on the ESP8266 with onboard PCB antenna and UART communications
